# Fritzing sketch Stepper Motor (saved by Fritzing 0.9.3b)

parts:
  Part1 = Arduino Uno (Rev3)
  MOTOR1 = 28BYJ-48 Stepper Motor
  X1 = X113647 Stepper Driver Board [package=board]

nets:
  N1: Part1.D8, X1.IN4
  N2: Part1.D9_PWM, X1.IN3
  N3: Part1.D10_PWM/SS, X1.IN2
  N4: Part1.D11_PWM/MOSI, X1.IN1
  N5: Part1.5V, X1.+V
  GND: Part1.GND, X1.GND
  N6: MOTOR1.BLUE, X1.BLUE
  N7: MOTOR1.PINK, X1.PINK
  N8: MOTOR1.RED, X1.RED
  N9: MOTOR1.ORANGE, X1.ORANGE
  N10: MOTOR1.YELLOW, X1.YELLOW

custom parts:
  28BYJ-48 Stepper Motor: 28BYJ-48 gear-reduction stepper motor (small)
  X113647 Stepper Driver Board: A common stepper motor driver board based on ULN2003APG darlington array
